# Fritzing sketch Circuit Diagram (saved by Fritzing 0.9.3b)
perfboards: 2

parts:
  Part1 = Arduino MKR1000
  R1 = Resistor [tolerance=±5% resistance=220 package=THT]
  S2 = Reed switch [package=THT]
  Power_plug1 = Power plug  # not connected
  S1 = Reed switch [package=THT]
  U1 = Sharp PC817 [package=THT]

nets:
  N1: Part1.D6, S1.pin_2
  N2: Part1.D7, S2.pin_2
  N3: Part1.D10_MISO, U1.Pin_4
  N4: R1.Pin_0, U1.Pin_1

notes:
  2x Relay Board
  > Light Input
  > Door Button
  > Light Switch

custom parts:
  Arduino MKR1000: MKR1000 is a powerful board that combines the functionality of the Zero and the Wi-Fi Shield. It is the ideal solution for makers wanting to design IoT projects with minimal previous experience in networking
